# Fritzing sketch Arduino Countdown Timer (saved by Fritzing 0.7.5b)
stripboards: 1

parts:
  R1 = Resistor [tolerance=±5% resistance=10k package=THT]
  Arduino1 = Arduino
  S1 = Pushbutton [package="[THT]"]
  LCD1 = LCD screen
  R2 = Trimmer Potentiometer [maximum_resistance=10kΩ package=THT]

nets:
  GND: R1.Pin_0, Arduino1.GND, LCD1.LED-, R2.leg1
  5V: R1.Pin_1, Arduino1.+5V, S1.Pin_3, S1.Pin_4, R2.leg2
  N1: Arduino1.D11, Arduino1.D9
  N2: Arduino1.D2, S1.Pin_1, S1.Pin_2
  N3: LCD1.V0, R2.wiper

notes:
  Arduino Countdown Timer, Arduino Project to display a countdown timer until our Holidays!, 0.1
